// Logisim project main.circ as structural Verilog: 7 circuits, main circuit main
module main (
  input  in_1,
  input  in_2,
  input  [4:0] in_3,
  input  [31:0] in_4,
  input  [7:0] in_5,
  input  [7:0] in_6
);

  wire clock_1_out;
  wire [31:0] videobuffer_1_out_8, videobuffer_1_out_9, videobuffer_1_out_10, videobuffer_1_out_11,
       videobuffer_1_out_12, videobuffer_1_out_13, videobuffer_1_out_14, videobuffer_1_out_15,
       videobuffer_1_out_16, videobuffer_1_out_17, videobuffer_1_out_18, videobuffer_1_out_19,
       videobuffer_1_out_20, videobuffer_1_out_21, videobuffer_1_out_22, videobuffer_1_out_23,
       videobuffer_1_out_24, videobuffer_1_out_25, videobuffer_1_out_26, videobuffer_1_out_27,
       videobuffer_1_out_28, videobuffer_1_out_29, videobuffer_1_out_30, videobuffer_1_out_31,
       videobuffer_1_out_32, videobuffer_1_out_33, videobuffer_1_out_34, videobuffer_1_out_35,
       videobuffer_1_out_36, videobuffer_1_out_37, videobuffer_1_out_38, videobuffer_1_out_39;

  // Probe on in_3
  videobuffer videobuffer_1 (
    .line_adr(in_3), .new_line(in_4), .out_8(videobuffer_1_out_8), .out_9(videobuffer_1_out_9),
    .out_10(videobuffer_1_out_10), .out_11(videobuffer_1_out_11), .out_12(videobuffer_1_out_12),
    .out_13(videobuffer_1_out_13), .out_14(videobuffer_1_out_14), .out_15(videobuffer_1_out_15),
    .out_16(videobuffer_1_out_16), .out_17(videobuffer_1_out_17), .out_18(videobuffer_1_out_18),
    .out_19(videobuffer_1_out_19), .out_20(videobuffer_1_out_20), .out_21(videobuffer_1_out_21),
    .out_22(videobuffer_1_out_22), .out_23(videobuffer_1_out_23), .out_24(videobuffer_1_out_24),
    .out_25(videobuffer_1_out_25), .out_26(videobuffer_1_out_26), .out_27(videobuffer_1_out_27),
    .out_28(videobuffer_1_out_28), .out_29(videobuffer_1_out_29), .out_30(videobuffer_1_out_30),
    .out_31(videobuffer_1_out_31), .out_32(videobuffer_1_out_32), .out_33(videobuffer_1_out_33),
    .out_34(videobuffer_1_out_34), .out_35(videobuffer_1_out_35), .out_36(videobuffer_1_out_36),
    .out_37(videobuffer_1_out_37), .out_38(videobuffer_1_out_38), .out_39(videobuffer_1_out_39), .sur(in_6),
    .born(in_5), .cl(clock_1_out), .start_stop(in_1), .out_ctrl(in_2));
  DotMatrix #(.inputtype("row"), .matrixcols(32), .matrixrows(32)) dotmatrix_1 (
    .row0(videobuffer_1_out_8), .row1(videobuffer_1_out_9), .row2(videobuffer_1_out_10),
    .row3(videobuffer_1_out_11), .row4(videobuffer_1_out_12), .row5(videobuffer_1_out_13),
    .row6(videobuffer_1_out_14), .row7(videobuffer_1_out_15), .row8(videobuffer_1_out_16),
    .row9(videobuffer_1_out_17), .row10(videobuffer_1_out_18), .row11(videobuffer_1_out_19),
    .row12(videobuffer_1_out_20), .row13(videobuffer_1_out_21), .row14(videobuffer_1_out_22),
    .row15(videobuffer_1_out_23), .row16(videobuffer_1_out_24), .row17(videobuffer_1_out_25),
    .row18(videobuffer_1_out_26), .row19(videobuffer_1_out_27), .row20(videobuffer_1_out_28),
    .row21(videobuffer_1_out_29), .row22(videobuffer_1_out_30), .row23(videobuffer_1_out_31),
    .row24(videobuffer_1_out_32), .row25(videobuffer_1_out_33), .row26(videobuffer_1_out_34),
    .row27(videobuffer_1_out_35), .row28(videobuffer_1_out_36), .row29(videobuffer_1_out_37),
    .row30(videobuffer_1_out_38), .row31(videobuffer_1_out_39));
  Clock clock_1 (.out(clock_1_out));
endmodule

module \cell  (
  input  [7:0] around,
  input  [7:0] born_rule,
  input  [7:0] survival_rule,
  input  clock,
  input  out_force,
  input  out_control,
  output state
);

  wire and_1_out, check_rules_1_born, check_rules_1_survive, controlled_buffer_1_out,
       controlled_inverter_1_out, or_1_out;
  wire [3:0] bitadder_1_out;

  BitAdder bitadder_1 (.in0(around), .out(bitadder_1_out));
  assign controlled_buffer_1_out = out_control ? out_force : 1'bz;  // Controlled_Buffer controlled_buffer_1
  assign controlled_inverter_1_out = out_control ? ~out_force : 1'bz;  // Controlled_Inverter controlled_inverter_1
  check_rules check_rules_1 (
    .count(bitadder_1_out), .born_rule(born_rule), .survival_rule(survival_rule), .Born(check_rules_1_born),
    .survive(check_rules_1_survive));
  D_Flip_Flop d_ff_1 (
    .clk(clock), .D(or_1_out), .Q(state), .preset(controlled_buffer_1_out), .reset(controlled_inverter_1_out));  // open: Qn, en
  and and_1 (and_1_out, check_rules_1_survive, state);
  or or_1 (or_1_out, check_rules_1_born, and_1_out);
endmodule

module line (
  input  [7:0] survival_rules,
  input  [7:0] born_rules,
  input  clock,
  input  out_ctrl,
  input  [31:0] up,
  input  [31:0] \force ,
  input  [31:0] down,
  output [31:0] output_up,
  output [31:0] output_down,
  output [31:0] output_main
);

  \cell  cell_1 (
    .around({up[0], down[0], up[1], down[1], up[31], down[31], output_down[31], output_down[1]}),
    .born_rule(born_rules), .survival_rule(survival_rules), .clock(clock), .state(output_down[0]),
    .out_force(\force [0]), .out_control(out_ctrl));
  \cell  cell_2 (
    .around({up[7], down[7], up[8], down[8], up[9], down[9], output_down[7], output_down[9]}),
    .born_rule(born_rules), .survival_rule(survival_rules), .clock(clock), .state(output_down[8]),
    .out_force(\force [8]), .out_control(out_ctrl));
  \cell  cell_3 (
    .around({up[15], down[15], up[16], down[16], up[17], down[17], output_down[15], output_down[17]}),
    .born_rule(born_rules), .survival_rule(survival_rules), .clock(clock), .state(output_down[16]),
    .out_force(\force [16]), .out_control(out_ctrl));
  \cell  cell_4 (
    .around({up[23], down[23], up[24], down[24], up[25], down[25], output_down[23], output_down[25]}),
    .born_rule(born_rules), .survival_rule(survival_rules), .clock(clock), .state(output_down[24]),
    .out_force(\force [24]), .out_control(out_ctrl));
  \cell  cell_5 (
    .around({up[0], down[0], up[1], down[1], up[2], down[2], output_down[0], output_down[2]}),
    .born_rule(born_rules), .survival_rule(survival_rules), .clock(clock), .state(output_down[1]),
    .out_force(\force [1]), .out_control(out_ctrl));
  \cell  cell_6 (
    .around({up[8], down[8], up[9], down[9], up[10], down[10], output_down[8], output_down[10]}),
    .born_rule(born_rules), .survival_rule(survival_rules), .clock(clock), .state(output_down[9]),
    .out_force(\force [9]), .out_control(out_ctrl));
  \cell  cell_7 (
    .around({up[16], down[16], up[17], down[17], up[18], down[18], output_down[16], output_down[18]}),
    .born_rule(born_rules), .survival_rule(survival_rules), .clock(clock), .state(output_down[17]),
    .out_force(\force [17]), .out_control(out_ctrl));
  \cell  cell_8 (
    .around({up[24], down[24], up[25], down[25], up[26], down[26], output_down[24], output_down[26]}),
    .born_rule(born_rules), .survival_rule(survival_rules), .clock(clock), .state(output_down[25]),
    .out_force(\force [25]), .out_control(out_ctrl));
  \cell  cell_9 (
    .around({up[1], down[1], up[2], down[2], up[3], down[3], output_down[1], output_down[3]}),
    .born_rule(born_rules), .survival_rule(survival_rules), .clock(clock), .state(output_down[2]),
    .out_force(\force [2]), .out_control(out_ctrl));
  \cell  cell_10 (
    .around({up[9], down[9], up[10], down[10], up[11], down[11], output_down[9], output_down[11]}),
    .born_rule(born_rules), .survival_rule(survival_rules), .clock(clock), .state(output_down[10]),
    .out_force(\force [10]), .out_control(out_ctrl));
  \cell  cell_11 (
    .around({up[17], down[17], up[18], down[18], up[19], down[19], output_down[17], output_down[19]}),
    .born_rule(born_rules), .survival_rule(survival_rules), .clock(clock), .state(output_down[18]),
    .out_force(\force [18]), .out_control(out_ctrl));
  \cell  cell_12 (
    .around({up[25], down[25], up[26], down[26], up[27], down[27], output_down[25], output_down[27]}),
    .born_rule(born_rules), .survival_rule(survival_rules), .clock(clock), .state(output_down[26]),
    .out_force(\force [26]), .out_control(out_ctrl));
  \cell  cell_13 (
    .around({up[2], down[2], up[3], down[3], up[4], down[4], output_down[2], output_down[4]}),
    .born_rule(born_rules), .survival_rule(survival_rules), .clock(clock), .state(output_down[3]),
    .out_force(\force [3]), .out_control(out_ctrl));
  \cell  cell_14 (
    .around({up[10], down[10], up[11], down[11], up[12], down[12], output_down[10], output_down[12]}),
    .born_rule(born_rules), .survival_rule(survival_rules), .clock(clock), .state(output_down[11]),
    .out_force(\force [11]), .out_control(out_ctrl));
  \cell  cell_15 (
    .around({up[18], down[18], up[19], down[19], up[20], down[20], output_down[18], output_down[20]}),
    .born_rule(born_rules), .survival_rule(survival_rules), .clock(clock), .state(output_down[19]),
    .out_force(\force [19]), .out_control(out_ctrl));
  \cell  cell_16 (
    .around({up[26], down[26], up[27], down[27], up[28], down[28], output_down[26], output_down[28]}),
    .born_rule(born_rules), .survival_rule(survival_rules), .clock(clock), .state(output_down[27]),
    .out_force(\force [27]), .out_control(out_ctrl));
  \cell  cell_17 (
    .around({up[3], down[3], up[4], down[4], up[5], down[5], output_down[3], output_down[5]}),
    .born_rule(born_rules), .survival_rule(survival_rules), .clock(clock), .state(output_down[4]),
    .out_force(\force [4]), .out_control(out_ctrl));
  \cell  cell_18 (
    .around({up[11], down[11], up[12], down[12], up[13], down[13], output_down[11], output_down[13]}),
    .born_rule(born_rules), .survival_rule(survival_rules), .clock(clock), .state(output_down[12]),
    .out_force(\force [12]), .out_control(out_ctrl));
  \cell  cell_19 (
    .around({up[19], down[19], up[20], down[20], up[21], down[21], output_down[19], output_down[21]}),
    .born_rule(born_rules), .survival_rule(survival_rules), .clock(clock), .state(output_down[20]),
    .out_force(\force [20]), .out_control(out_ctrl));
  \cell  cell_20 (
    .around({up[27], down[27], up[28], down[28], up[29], down[29], output_down[27], output_down[29]}),
    .born_rule(born_rules), .survival_rule(survival_rules), .clock(clock), .state(output_down[28]),
    .out_force(\force [28]), .out_control(out_ctrl));
  \cell  cell_21 (
    .around({up[4], down[4], up[5], down[5], up[6], down[6], output_down[4], output_down[6]}),
    .born_rule(born_rules), .survival_rule(survival_rules), .clock(clock), .state(output_down[5]),
    .out_force(\force [5]), .out_control(out_ctrl));
  \cell  cell_22 (
    .around({up[12], down[12], up[13], down[13], up[14], down[14], output_down[12], output_down[14]}),
    .born_rule(born_rules), .survival_rule(survival_rules), .clock(clock), .state(output_down[13]),
    .out_force(\force [13]), .out_control(out_ctrl));
  \cell  cell_23 (
    .around({up[20], down[20], up[21], down[21], up[22], down[22], output_down[20], output_down[22]}),
    .born_rule(born_rules), .survival_rule(survival_rules), .clock(clock), .state(output_down[21]),
    .out_force(\force [21]), .out_control(out_ctrl));
  \cell  cell_24 (
    .around({up[28], down[28], up[29], down[29], up[30], down[30], output_down[28], output_down[30]}),
    .born_rule(born_rules), .survival_rule(survival_rules), .clock(clock), .state(output_down[29]),
    .out_force(\force [29]), .out_control(out_ctrl));
  \cell  cell_25 (
    .around({up[5], down[5], up[6], down[6], up[7], down[7], output_down[5], output_down[7]}),
    .born_rule(born_rules), .survival_rule(survival_rules), .clock(clock), .state(output_down[6]),
    .out_force(\force [6]), .out_control(out_ctrl));
  \cell  cell_26 (
    .around({up[13], down[13], up[14], down[14], up[15], down[15], output_down[13], output_down[15]}),
    .born_rule(born_rules), .survival_rule(survival_rules), .clock(clock), .state(output_down[14]),
    .out_force(\force [14]), .out_control(out_ctrl));
  \cell  cell_27 (
    .around({up[21], down[21], up[22], down[22], up[23], down[23], output_down[21], output_down[23]}),
    .born_rule(born_rules), .survival_rule(survival_rules), .clock(clock), .state(output_down[22]),
    .out_force(\force [22]), .out_control(out_ctrl));
  \cell  cell_28 (
    .around({up[29], down[29], up[30], down[30], up[31], down[31], output_down[29], output_down[31]}),
    .born_rule(born_rules), .survival_rule(survival_rules), .clock(clock), .state(output_down[30]),
    .out_force(\force [30]), .out_control(out_ctrl));
  \cell  cell_29 (
    .around({up[6], down[6], up[7], down[7], up[8], down[8], output_down[6], output_down[8]}),
    .born_rule(born_rules), .survival_rule(survival_rules), .clock(clock), .state(output_down[7]),
    .out_force(\force [7]), .out_control(out_ctrl));
  \cell  cell_30 (
    .around({up[14], down[14], up[15], down[15], up[16], down[16], output_down[14], output_down[16]}),
    .born_rule(born_rules), .survival_rule(survival_rules), .clock(clock), .state(output_down[15]),
    .out_force(\force [15]), .out_control(out_ctrl));
  \cell  cell_31 (
    .around({up[22], down[22], up[23], down[23], up[24], down[24], output_down[22], output_down[24]}),
    .born_rule(born_rules), .survival_rule(survival_rules), .clock(clock), .state(output_down[23]),
    .out_force(\force [23]), .out_control(out_ctrl));
  \cell  cell_32 (
    .around({up[30], down[30], up[31], down[31], up[0], down[0], output_down[0], output_down[30]}),
    .born_rule(born_rules), .survival_rule(survival_rules), .clock(clock), .state(output_down[31]),
    .out_force(\force [31]), .out_control(out_ctrl));

  assign output_main = output_down;
  assign output_up = output_down;

  // Other names for the same wires on the sheet: d1 = down[1]; d9 = down[9]; d17 = down[17]; d25 = down[25];
  //   d2 = down[2]; d10 = down[10]; d18 = down[18]; d26 = down[26]; m3 = output_down[3]; output[31:0] = output_down;
  //   d3 = down[3]; p3 = up[3]; m11 = output_down[11]; d11 = down[11]; p11 = up[11]; m19 = output_down[19];
  //   d19 = down[19]; p19 = up[19]; m27 = output_down[27]; d27 = down[27]; p27 = up[27]; m4 = output_down[4];
  //   d4 = down[4]; p4 = up[4]; m12 = output_down[12]; d12 = down[12]; p12 = up[12]; m20 = output_down[20];
  //   d20 = down[20]; p20 = up[20]; m28 = output_down[28]; d28 = down[28]; p28 = up[28]; m7 = output_down[7];
  //   m5 = output_down[5]; d5 = down[5]; p5 = up[5]; m15 = output_down[15]; m13 = output_down[13]; d13 = down[13];
  //   p13 = up[13]; m23 = output_down[23]; m21 = output_down[21]; d21 = down[21]; p21 = up[21]; m31 = output_down[31];
  //   m29 = output_down[29]; d29 = down[29]; p29 = up[29]; m8 = output_down[8]; m6 = output_down[6]; d8 = down[8];
  //   p8 = up[8]; d7 = down[7]; p7 = up[7]; d6 = down[6]; p6 = up[6]; m16 = output_down[16]; m14 = output_down[14];
  //   d16 = down[16]; p16 = up[16]; d15 = down[15]; p15 = up[15]; d14 = down[14]; p14 = up[14]; m24 = output_down[24];
  //   m22 = output_down[22]; d24 = down[24]; p24 = up[24]; d23 = down[23]; p23 = up[23]; d22 = down[22]; p22 = up[22];
  //   m30 = output_down[30]; m0 = output_down[0]; d0 = down[0]; p0 = up[0]; d31 = down[31]; p31 = up[31];
  //   d30 = down[30]; p30 = up[30]; bor[7:0] = born_rules; cl = clock; ctrl = out_ctrl; u0 = \force [0];
  //   u1 = \force [1]; u2 = \force [2]; u3 = \force [3]; u4 = \force [4]; u5 = \force [5]; u6 = \force [6];
  //   u7 = \force [7]; u8 = \force [8]; u9 = \force [9]; u10 = \force [10]; u11 = \force [11]; u12 = \force [12];
  //   u13 = \force [13]; u14 = \force [14]; u15 = \force [15]; u16 = \force [16]; u17 = \force [17];
  //   u18 = \force [18]; u19 = \force [19]; u20 = \force [20]; u21 = \force [21]; u22 = \force [22];
  //   u23 = \force [23]; u24 = \force [24]; u25 = \force [25]; u26 = \force [26]; u27 = \force [27];
  //   u28 = \force [28]; u29 = \force [29]; u30 = \force [30]; u31 = \force [31]; m1 = output_down[1];
  //   m2 = output_down[2]; m9 = output_down[9]; m10 = output_down[10]; m17 = output_down[17]; m18 = output_down[18];
  //   m25 = output_down[25]; m26 = output_down[26]; sur[7:0] = survival_rules; p1 = up[1]; p2 = up[2]; p9 = up[9];
  //   p10 = up[10]; p17 = up[17]; p18 = up[18]; p25 = up[25]; p26 = up[26]
endmodule

module videobuffer (
  input  [7:0] sur,
  input  [7:0] born,
  input  cl,
  input  start_stop,
  input  out_ctrl,
  input  [4:0] line_adr,
  input  [31:0] new_line,
  output [31:0] out_8,
  output [31:0] out_9,
  output [31:0] out_10,
  output [31:0] out_11,
  output [31:0] out_12,
  output [31:0] out_13,
  output [31:0] out_14,
  output [31:0] out_15,
  output [31:0] out_16,
  output [31:0] out_17,
  output [31:0] out_18,
  output [31:0] out_19,
  output [31:0] out_20,
  output [31:0] out_21,
  output [31:0] out_22,
  output [31:0] out_23,
  output [31:0] out_24,
  output [31:0] out_25,
  output [31:0] out_26,
  output [31:0] out_27,
  output [31:0] out_28,
  output [31:0] out_29,
  output [31:0] out_30,
  output [31:0] out_31,
  output [31:0] out_32,
  output [31:0] out_33,
  output [31:0] out_34,
  output [31:0] out_35,
  output [31:0] out_36,
  output [31:0] out_37,
  output [31:0] out_38,
  output [31:0] out_39
);

  wire a0, a1, a2, a3, a4, a5, a6, a7, a8, a9, a10, a11, a12, a13, a14, a15, a16, a17, a18, a19, a20, a21,
       a22, a23, a24, a25, a26, a27, a28, a29, a30, a31, and_1_out, controlled_buffer_1_out, not_1_out;
  wire [31:0] c1, c2, line_1_output_down, line_2_output_down, line_2_output_up, line_3_output_down,
       line_3_output_up, line_4_output_down, line_4_output_up, line_5_output_down, line_5_output_up,
       line_6_output_down, line_6_output_up, line_7_output_down, line_7_output_up, line_8_output_down,
       line_8_output_up, line_9_output_down, line_9_output_up, line_10_output_down, line_10_output_up,
       line_11_output_down, line_11_output_up, line_12_output_down, line_12_output_up, line_13_output_down,
       line_13_output_up, line_14_output_down, line_14_output_up, line_15_output_down, line_15_output_up,
       line_16_output_down, line_16_output_up, line_17_output_down, line_17_output_up, line_18_output_down,
       line_18_output_up, line_19_output_down, line_19_output_up, line_20_output_down, line_20_output_up,
       line_21_output_down, line_21_output_up, line_22_output_down, line_22_output_up, line_23_output_down,
       line_23_output_up, line_24_output_down, line_24_output_up, line_25_output_down, line_25_output_up,
       line_26_output_down, line_26_output_up, line_27_output_down, line_27_output_up, line_28_output_down,
       line_28_output_up, line_29_output_down, line_29_output_up, line_30_output_down, line_30_output_up,
       line_31_output_down, line_31_output_up, line_32_output_up, u0, u1, u2, u3, u4, u5, u6, u7, u8, u9,
       u10, u11, u12, u13, u14, u15, u16, u17, u18, u19, u20, u21, u22, u23, u24, u25, u26, u27, u28, u29,
       u30, u31;

  line line_1 (
    .survival_rules(sur), .born_rules(born), .clock(controlled_buffer_1_out), .output_up(c1),
    .output_down(line_1_output_down), .up(c2), .\force (u0), .down(line_2_output_up), .output_main(out_8),
    .out_ctrl(a0));
  line line_2 (
    .survival_rules(sur), .born_rules(born), .clock(controlled_buffer_1_out), .output_up(line_2_output_up),
    .output_down(line_2_output_down), .up(line_1_output_down), .\force (u1), .down(line_3_output_up),
    .output_main(out_9), .out_ctrl(a1));
  line line_3 (
    .survival_rules(sur), .born_rules(born), .clock(controlled_buffer_1_out), .output_up(line_3_output_up),
    .output_down(line_3_output_down), .up(line_2_output_down), .\force (u2), .down(line_4_output_up),
    .output_main(out_10), .out_ctrl(a2));
  line line_4 (
    .survival_rules(sur), .born_rules(born), .clock(controlled_buffer_1_out), .output_up(line_4_output_up),
    .output_down(line_4_output_down), .up(line_3_output_down), .\force (u3), .down(line_5_output_up),
    .output_main(out_11), .out_ctrl(a3));
  line line_5 (
    .survival_rules(sur), .born_rules(born), .clock(controlled_buffer_1_out), .output_up(line_5_output_up),
    .output_down(line_5_output_down), .up(line_4_output_down), .\force (u4), .down(line_6_output_up),
    .output_main(out_12), .out_ctrl(a4));
  line line_6 (
    .survival_rules(sur), .born_rules(born), .clock(controlled_buffer_1_out), .output_up(line_6_output_up),
    .output_down(line_6_output_down), .up(line_5_output_down), .\force (u5), .down(line_7_output_up),
    .output_main(out_13), .out_ctrl(a5));
  line line_7 (
    .survival_rules(sur), .born_rules(born), .clock(controlled_buffer_1_out), .output_up(line_7_output_up),
    .output_down(line_7_output_down), .up(line_6_output_down), .\force (u6), .down(line_8_output_up),
    .output_main(out_14), .out_ctrl(a6));
  line line_8 (
    .survival_rules(sur), .born_rules(born), .clock(controlled_buffer_1_out), .output_up(line_8_output_up),
    .output_down(line_8_output_down), .up(line_7_output_down), .\force (u7), .down(line_9_output_up),
    .output_main(out_15), .out_ctrl(a7));
  line line_9 (
    .survival_rules(sur), .born_rules(born), .clock(controlled_buffer_1_out), .output_up(line_9_output_up),
    .output_down(line_9_output_down), .up(line_8_output_down), .\force (u8), .down(line_10_output_up),
    .output_main(out_16), .out_ctrl(a8));
  line line_10 (
    .survival_rules(sur), .born_rules(born), .clock(controlled_buffer_1_out), .output_up(line_10_output_up),
    .output_down(line_10_output_down), .up(line_9_output_down), .\force (u9), .down(line_11_output_up),
    .output_main(out_17), .out_ctrl(a9));
  line line_11 (
    .survival_rules(sur), .born_rules(born), .clock(controlled_buffer_1_out), .output_up(line_11_output_up),
    .output_down(line_11_output_down), .up(line_10_output_down), .\force (u10), .down(line_12_output_up),
    .output_main(out_18), .out_ctrl(a10));
  line line_12 (
    .survival_rules(sur), .born_rules(born), .clock(controlled_buffer_1_out), .output_up(line_12_output_up),
    .output_down(line_12_output_down), .up(line_11_output_down), .\force (u11), .down(line_13_output_up),
    .output_main(out_19), .out_ctrl(a11));
  line line_13 (
    .survival_rules(sur), .born_rules(born), .clock(controlled_buffer_1_out), .output_up(line_13_output_up),
    .output_down(line_13_output_down), .up(line_12_output_down), .\force (u12), .down(line_14_output_up),
    .output_main(out_20), .out_ctrl(a12));
  line line_14 (
    .survival_rules(sur), .born_rules(born), .clock(controlled_buffer_1_out), .output_up(line_14_output_up),
    .output_down(line_14_output_down), .up(line_13_output_down), .\force (u13), .down(line_15_output_up),
    .output_main(out_21), .out_ctrl(a13));
  line line_15 (
    .survival_rules(sur), .born_rules(born), .clock(controlled_buffer_1_out), .output_up(line_15_output_up),
    .output_down(line_15_output_down), .up(line_14_output_down), .\force (u14), .down(line_16_output_up),
    .output_main(out_22), .out_ctrl(a14));
  line line_16 (
    .survival_rules(sur), .born_rules(born), .clock(controlled_buffer_1_out), .output_up(line_16_output_up),
    .output_down(line_16_output_down), .up(line_15_output_down), .\force (u15), .down(line_17_output_up),
    .output_main(out_23), .out_ctrl(a15));
  line line_17 (
    .survival_rules(sur), .born_rules(born), .clock(controlled_buffer_1_out), .output_up(line_17_output_up),
    .output_down(line_17_output_down), .up(line_16_output_down), .\force (u16), .down(line_18_output_up),
    .output_main(out_24), .out_ctrl(a16));
  line line_18 (
    .survival_rules(sur), .born_rules(born), .clock(controlled_buffer_1_out), .output_up(line_18_output_up),
    .output_down(line_18_output_down), .up(line_17_output_down), .\force (u17), .down(line_19_output_up),
    .output_main(out_25), .out_ctrl(a17));
  line line_19 (
    .survival_rules(sur), .born_rules(born), .clock(controlled_buffer_1_out), .output_up(line_19_output_up),
    .output_down(line_19_output_down), .up(line_18_output_down), .\force (u18), .down(line_20_output_up),
    .output_main(out_26), .out_ctrl(a18));
  line line_20 (
    .survival_rules(sur), .born_rules(born), .clock(controlled_buffer_1_out), .output_up(line_20_output_up),
    .output_down(line_20_output_down), .up(line_19_output_down), .\force (u19), .down(line_21_output_up),
    .output_main(out_27), .out_ctrl(a19));
  line line_21 (
    .survival_rules(sur), .born_rules(born), .clock(controlled_buffer_1_out), .output_up(line_21_output_up),
    .output_down(line_21_output_down), .up(line_20_output_down), .\force (u20), .down(line_22_output_up),
    .output_main(out_28), .out_ctrl(a20));
  line line_22 (
    .survival_rules(sur), .born_rules(born), .clock(controlled_buffer_1_out), .output_up(line_22_output_up),
    .output_down(line_22_output_down), .up(line_21_output_down), .\force (u21), .down(line_23_output_up),
    .output_main(out_29), .out_ctrl(a21));
  line line_23 (
    .survival_rules(sur), .born_rules(born), .clock(controlled_buffer_1_out), .output_up(line_23_output_up),
    .output_down(line_23_output_down), .up(line_22_output_down), .\force (u22), .down(line_24_output_up),
    .output_main(out_30), .out_ctrl(a22));
  line line_24 (
    .survival_rules(sur), .born_rules(born), .clock(controlled_buffer_1_out), .output_up(line_24_output_up),
    .output_down(line_24_output_down), .up(line_23_output_down), .\force (u23), .down(line_25_output_up),
    .output_main(out_31), .out_ctrl(a23));
  line line_25 (
    .survival_rules(sur), .born_rules(born), .clock(controlled_buffer_1_out), .output_up(line_25_output_up),
    .output_down(line_25_output_down), .up(line_24_output_down), .\force (u24), .down(line_26_output_up),
    .output_main(out_32), .out_ctrl(a24));
  line line_26 (
    .survival_rules(sur), .born_rules(born), .clock(controlled_buffer_1_out), .output_up(line_26_output_up),
    .output_down(line_26_output_down), .up(line_25_output_down), .\force (u25), .down(line_27_output_up),
    .output_main(out_33), .out_ctrl(a25));
  line line_27 (
    .survival_rules(sur), .born_rules(born), .clock(controlled_buffer_1_out), .output_up(line_27_output_up),
    .output_down(line_27_output_down), .up(line_26_output_down), .\force (u26), .down(line_28_output_up),
    .output_main(out_34), .out_ctrl(a26));
  line line_28 (
    .survival_rules(sur), .born_rules(born), .clock(controlled_buffer_1_out), .output_up(line_28_output_up),
    .output_down(line_28_output_down), .up(line_27_output_down), .\force (u27), .down(line_29_output_up),
    .output_main(out_35), .out_ctrl(a27));
  line line_29 (
    .survival_rules(sur), .born_rules(born), .clock(controlled_buffer_1_out), .output_up(line_29_output_up),
    .output_down(line_29_output_down), .up(line_28_output_down), .\force (u28), .down(line_30_output_up),
    .output_main(out_36), .out_ctrl(a28));
  line line_30 (
    .survival_rules(sur), .born_rules(born), .clock(controlled_buffer_1_out), .output_up(line_30_output_up),
    .output_down(line_30_output_down), .up(line_29_output_down), .\force (u29), .down(line_31_output_up),
    .output_main(out_37), .out_ctrl(a29));
  line line_31 (
    .survival_rules(sur), .born_rules(born), .clock(controlled_buffer_1_out), .output_up(line_31_output_up),
    .output_down(line_31_output_down), .up(line_30_output_down), .\force (u30), .down(line_32_output_up),
    .output_main(out_38), .out_ctrl(a30));
  line line_32 (
    .survival_rules(sur), .born_rules(born), .clock(controlled_buffer_1_out), .output_up(line_32_output_up),
    .output_down(c2), .up(line_31_output_down), .\force (u31), .down(c1), .output_main(out_39), .out_ctrl(a31));
  assign controlled_buffer_1_out = and_1_out ? cl : 1'bz;  // Controlled_Buffer controlled_buffer_1
  Pull_Resistor pull_resistor_1 (.node(controlled_buffer_1_out));
  and and_1 (and_1_out, start_stop, not_1_out);
  Demultiplexer #(.select(5), .width(32), .enable("false")) demultiplexer_1 (
    .out0(u0), .out1(u1), .out2(u2), .out3(u3), .out4(u4), .out5(u5), .out6(u6), .out7(u7), .out8(u8),
    .out9(u9), .out10(u10), .out11(u11), .out12(u12), .out13(u13), .out14(u14), .out15(u15), .out16(u16),
    .out17(u17), .out18(u18), .out19(u19), .out20(u20), .out21(u21), .out22(u22), .out23(u23), .out24(u24),
    .out25(u25), .out26(u26), .out27(u27), .out28(u28), .out29(u29), .out30(u30), .out31(u31), .in(new_line),
    .sel(line_adr));
  Demultiplexer #(.select(5), .enable("false")) demultiplexer_2 (
    .out0(a0), .out1(a1), .out2(a2), .out3(a3), .out4(a4), .out5(a5), .out6(a6), .out7(a7), .out8(a8),
    .out9(a9), .out10(a10), .out11(a11), .out12(a12), .out13(a13), .out14(a14), .out15(a15), .out16(a16),
    .out17(a17), .out18(a18), .out19(a19), .out20(a20), .out21(a21), .out22(a22), .out23(a23), .out24(a24),
    .out25(a25), .out26(a26), .out27(a27), .out28(a28), .out29(a29), .out30(a30), .out31(a31), .in(out_ctrl),
    .sel(line_adr));
  not not_1 (not_1_out, out_ctrl);

  // Other names for the same wires on the sheet: adr[4:0] = line_adr; ctrl = out_ctrl; o0[31:0] = out_8;
  //   o1[31:0] = out_9; o2[31:0] = out_10; o3[31:0] = out_11; o4[31:0] = out_12; o5[31:0] = out_13; o6[31:0] = out_14;
  //   o7[31:0] = out_15; o8[31:0] = out_16; o9[31:0] = out_17; o10[31:0] = out_18; o11[31:0] = out_19;
  //   o12[31:0] = out_20; o13[31:0] = out_21; o14[31:0] = out_22; o15[31:0] = out_23; o16[31:0] = out_24;
  //   o17[31:0] = out_25; o18[31:0] = out_26; o19[31:0] = out_27; o20[31:0] = out_28; o21[31:0] = out_29;
  //   o22[31:0] = out_30; o23[31:0] = out_31; o24[31:0] = out_32; o25[31:0] = out_33; o26[31:0] = out_34;
  //   o27[31:0] = out_35; o28[31:0] = out_36; o29[31:0] = out_37; o30[31:0] = out_38; o31[31:0] = out_39
endmodule

module check_rules (
  input  [3:0] count,
  input  [7:0] born_rule,
  input  [7:0] survival_rule,
  output Born,
  output survive
);

  Multiplexer #(.select(4), .enable("false")) multiplexer_1 (
    .in0(1'b0), .in1(born_rule[0]), .in2(born_rule[1]), .in3(born_rule[2]), .in4(born_rule[3]),
    .in5(born_rule[4]), .in6(born_rule[5]), .in7(born_rule[6]), .in8(born_rule[7]), .out(Born), .sel(count));  // open: in9, in10, in11, in12, in13, in14, in15
  Multiplexer #(.select(4), .enable("false")) multiplexer_2 (
    .in0(1'b0), .in1(survival_rule[0]), .in2(survival_rule[1]), .in3(survival_rule[2]),
    .in4(survival_rule[3]), .in5(survival_rule[4]), .in6(survival_rule[5]), .in7(survival_rule[6]),
    .in8(survival_rule[7]), .out(survive), .sel(count));  // open: in9, in10, in11, in12, in13, in14, in15
endmodule

module test (
  input  [7:0] around,
  input  [7:0] born_rule,
  input  [7:0] survival_rule,
  input  clock,
  input  outside,
  input  out_control,
  output state
);

  wire and_1_out, check_rules_1_born, check_rules_1_survive, controlled_buffer_1_out,
       controlled_inverter_1_out, or_1_out;
  wire [3:0] bitadder_1_out;

  BitAdder bitadder_1 (.in0(around), .out(bitadder_1_out));
  assign controlled_buffer_1_out = out_control ? outside : 1'bz;  // Controlled_Buffer controlled_buffer_1
  assign controlled_inverter_1_out = out_control ? ~outside : 1'bz;  // Controlled_Inverter controlled_inverter_1
  check_rules check_rules_1 (
    .count(bitadder_1_out), .born_rule(born_rule), .survival_rule(survival_rule), .Born(check_rules_1_born),
    .survive(check_rules_1_survive));
  D_Flip_Flop d_ff_1 (
    .clk(clock), .D(or_1_out), .Q(state), .preset(controlled_buffer_1_out), .reset(controlled_inverter_1_out));  // open: Qn, en
  and and_1 (and_1_out, check_rules_1_survive, state);
  or or_1 (or_1_out, check_rules_1_born, and_1_out);
endmodule

module ProcessorLogic (
);

  wire button_1_out, cdm_16_1_p1, cdm_16_1_p2, cdm_16_1_p3, cdm_16_1_p4, cdm_16_1_p5, cdm_16_1_p6,
       cdm_16_1_p7, cdm_16_1_p8, cdm_16_1_p9, cdm_16_1_p10, cdm_16_1_p11, cdm_16_1_p12, clock_2_out, mem,
       not_1_out, read, word;
  wire [15:0] address_bus, controlled_buffer_2_out, data_bus, ram_1_p3;

  // Probe on cdm_16_1_p9
  // Probe on cdm_16_1_p8
  // Probe on cdm_16_1_p7
  // Probe on cdm_16_1_p6
  // Probe on cdm_16_1_p5
  // Probe on cdm_16_1_p4
  // Probe on cdm_16_1_p2
  // Probe on cdm_16_1_p1
  // CdM_16 cdm_16_1: pin names not known; wires that end beside it: cdm_16_1_p1, cdm_16_1_p2, cdm_16_1_p3, cdm_16_1_p4, cdm_16_1_p5, cdm_16_1_p6, cdm_16_1_p7, cdm_16_1_p8, cdm_16_1_p9, cdm_16_1_p10, cdm_16_1_p11, cdm_16_1_p12, mem, read, word, address_bus
  Clock clock_1 (.out(cdm_16_1_p3));
  // Probe on cdm_16_1_p10
  // Probe on cdm_16_1_p11
  // Probe on cdm_16_1_p12
  assign data_bus = not_1_out ? ram_1_p3 : 16'bz;  // Controlled_Buffer controlled_buffer_1
  not not_1 (not_1_out, read);
  assign controlled_buffer_2_out = read ? data_bus : 16'bz;  // Controlled_Buffer controlled_buffer_2
  Button button_1 (.out(button_1_out));
  Clock clock_2 (.out(clock_2_out));
  // Debugger debugger_1: pin names not known
  // RAM ram_1: pin names not known; wires that end beside it: address_bus, word, ram_1_p3, controlled_buffer_2_out, mem, clock_2_out, read, button_1_out, data_bus

  // Notes on the sheet:
  //   r7/fp
  //   r6
  //   r5
  //   r4
  //   r3
  //   r2
  //   r1
  //   r0
  //   pc
  //   sp
  //   ps
endmodule
